# Fritzing sketch Orthomus (UNO) (Latest Version) (saved by Fritzing 0.9.3b)
perfboards: 3

parts:
  U1 = LIPO-2000mAh [package=lipo-2000]
  L1 = Solenoid
  L2 = Solenoid
  U2 = 2-Channel 5v Relay Shield [package=relay-2ch5v10a]
  Part3 = Arduino Uno (Rev3)
  Grove1 = Grove - SPDT Relay(30A) [part_number=103020012]
  BAT1 = BC9VPC [package=bc9vpc]
  7805 = Voltage Regulator [package=to220-igo]  # not connected
  C2 = Electrolytic Capacitor [capacitance=100μF package="0807 [SMD, electrolytic]"]  # not connected
  C3 = Ceramic Capacitor [capacitance="100 nF" package="0805 [SMD, multilayer]"]  # not connected
  J1 = female pin header, 2 pins [form="♀ (female)"]  # not connected
  J2 = female pin header, 2 pins [form="♀ (female)"]
  J3 = female pin header, 2 pins [form="♀ (female)"]
  J4 = female pin header, 2 pins [form="♀ (female)"]
  J5 = female pin header, 2 pins [form="♀ (female)"]  # not connected
  J6 = female pin header, 2 pins [form="♀ (female)"]
  J7 = female pin header, 2 pins [form="♀ (female)"]
  J8 = female pin header, 2 pins [form="♀ (female)"]  # not connected
  J9 = female pin header, 2 pins [form="♀ (female)"]  # not connected
  J10 = female pin header, 2 pins [form="♀ (female)"]  # not connected
  J12 = Basic Servo  # not connected
  J13 = female pin header, 2 pins [form="♀ (female)"]
  J14 = female pin header, 2 pins [form="♀ (female)"]  # not connected
  J15 = female pin header, 2 pins [form="♀ (female)"]  # not connected
  J16 = female pin header, 2 pins [form="♀ (female)"]  # not connected
  J17 = female pin header, 2 pins [form="♀ (female)"]  # not connected
  J18 = female pin header, 2 pins [form="♀ (female)"]  # not connected
  J19 = Screw terminal - 2 pins [package=THT]
  J20 = Screw terminal - 2 pins [package=THT]  # not connected
  J21 = Screw terminal - 2 pins [package=THT]
  J22 = Screw terminal - 2 pins [package=THT]
  J23 = Screw terminal - 2 pins [package=THT]
  R4 = Resistor [tolerance=±5% resistance=10k package=THT]  # not connected
  R5 = Resistor [tolerance=±5% resistance=10k package=THT]  # not connected
  R6 = Resistor [tolerance=±5% resistance=10k package=THT]  # not connected
  S4 = Pushbutton [package="[THT]"]
  S5 = Pushbutton [package="[THT]"]
  S6 = Pushbutton [package="[THT]"]
  J24 = female pin header, 2 pins [form="♀ (female)"]
  J25 = female pin header, 2 pins [form="♀ (female)"]
  J26 = female pin header, 2 pins [form="♀ (female)"]
  J27 = female pin header, 2 pins [form="♀ (female)"]  # not connected
  J28 = female pin header, 2 pins [form="♀ (female)"]  # not connected
  J29 = female pin header, 2 pins [form="♀ (female)"]  # not connected
  J30 = female pin header, 2 pins [form="♀ (female)"]
  J31 = female pin header, 2 pins [form="♀ (female)"]  # not connected
  J32 = female pin header, 2 pins [form="♀ (female)"]  # not connected
  J33 = female pin header, 2 pins [form="♀ (female)"]  # not connected
  J34 = female pin header, 2 pins [form="♀ (female)"]
  J11 = Basic Servo  # not connected

nets:
  N1: U1.+, Grove1.RelayNO
  N2: U1.-, J21.pin1
  N3: L1.pin1, J23.pin1
  N4: L1.pin2, U2.K1-On
  N5: L2.pin1, J22.pin1
  N6: L2.pin2, U2.K2-On
  VCC: U2.VCC, Grove1.VCC, J6.pin1, J7.pin2
  N7: U2.IN1, Part3.D2
  N8: U2.IN2, Part3.D7
  N9: U2.K1-In, J23.pin2
  N10: U2.K2-In, J22.pin2
  N11: U2.JD-GND, J4.pin1
  N12: Part3.D9_PWM, Grove1.SIG
  N13: Part3.D3_PWM, J25.pin2
  N14: Part3.D5_PWM, J26.pin2
  N15: Part3.D6_PWM, J24.pin2
  N16: Part3.GND, J4.pin2, J13.pin1
  N17: Grove1.GND, J3.pin2
  N18: Grove1.RelayCom, J21.pin2
  N19: BAT1.V+, J19.pin2
  N20: BAT1.V-, J19.pin1
  N21: J2.pin2, J34.pin2
  N22: J7.pin1, J30.pin2
  N23: S4.Pin_1, S4.Pin_2
  N24: S4.Pin_3, S4.Pin_4
  N25: S5.Pin_1, S5.Pin_2
  N26: S5.Pin_3, S5.Pin_4
  N27: S6.Pin_1, S6.Pin_2
  N28: S6.Pin_3, S6.Pin_4

custom parts:
  2-Channel 5v Relay Shield: 2 Channel 5v Relay Shield w. 2x SPD-06VDC-SD-C
  Grove - SPDT Relay(30A): TheSPDT Relay(30A) is a high quality Single Pole Double Throw Relay(SPDT).The Relay consist of a coil, 1 common terminal, 1 normally closed(NC) terminal and one normally open(NO) terminal. When the coil of the relay is at rest (not energized), the common terminal and the normally closed terminal have continuity. When the coil is energized, the common terminal and the normally open terminal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
